# Fritzing sketch Project2 (saved by Fritzing 0.9.1b)
breadboards: 1

parts:
  Raspberry_Pi1 = Raspberry Pi B+
  S1 = Momentary Switch [package=ksa_sealed_tac_switch]

nets:
  N1: Raspberry_Pi1.GPIO14, S1.3
  N2: Raspberry_Pi1.GND, S1.1
